// Digital circuit IR.dig as structural Verilog
module IR (
  input  clk,
  input  [3:0] DRAM,
  input  [1:0] Load__LD,
  output [3:0] Output
);

  wire [3:0] multiplexer_1_out;

  Multiplexer #(.Selector_Bits(2), .Bits(4)) multiplexer_1 (
    .sel(Load__LD), .in_0(4'b0000), .in_1(DRAM), .in_2(Output), .in_3(4'b1111), .out(multiplexer_1_out));
  D_FF d_ff_1 (.D(multiplexer_1_out[3]), .C(clk), .Q(Output[3]));  // open: nQ
  D_FF d_ff_2 (.D(multiplexer_1_out[2]), .C(clk), .Q(Output[2]));  // open: nQ
  D_FF d_ff_3 (.D(multiplexer_1_out[1]), .C(clk), .Q(Output[1]));  // open: nQ
  D_FF d_ff_4 (.D(multiplexer_1_out[0]), .C(clk), .Q(Output[0]));  // open: nQ

  // Notes on the sheet:
  //   Load__LD: 0 -> Clear
  //   1 -> Store Input
  //   2 -> Load
  //   3 -> Set F
endmodule
