// Digital circuit control_RType_InClass.dig as structural Verilog
module control_RType_InClass (
  input  Clock,
  output [4:0] States,
  output IR_HI_Write,
  output IR_LO_Write,
  output WriteBack,
  output Increment_PC
);

  D_FF #(.Default(1)) IF1 (.D(States[4]), .C(Clock), .Q(IR_HI_Write));  // open: nQ
  D_FF IF2 (.D(IR_HI_Write), .C(Clock), .Q(IR_LO_Write));  // open: nQ
  D_FF Decode (.D(IR_LO_Write), .C(Clock), .Q(States[2]));  // open: nQ
  D_FF Execute (.D(States[2]), .C(Clock), .Q(States[3]));  // open: nQ
  D_FF u_WriteBack (.D(States[3]), .C(Clock), .Q(States[4]));  // open: nQ
  or or_1 (Increment_PC, IR_HI_Write, States[4]);

  assign States[1:0] = {IR_LO_Write, IR_HI_Write};
  assign WriteBack = States[4];
endmodule
