// Digital circuit hw1_full_adder.dig as structural Verilog
module hw1_full_adder (
  input  A0,
  input  B0,
  input  Cin,
  input  A1,
  input  B1,
  input  A2,
  input  B2,
  input  A3,
  input  B3,
  output S0,
  output Cout,
  output S1,
  output C2,
  output S2,
  output C3,
  output S3,
  output C4
);

  wire and_1_out, and_2_out, and_3_out, and_4_out, and_5_out, and_6_out, and_7_out, and_8_out, xor_1_out,
       xor_2_out, xor_3_out, xor_4_out;

  xor xor_1 (xor_1_out, A0, B0);
  and and_1 (and_1_out, A0, B0);
  xor xor_2 (xor_2_out, A1, B1);
  and and_2 (and_2_out, A1, B1);
  xor xor_3 (xor_3_out, A2, B2);
  xor xor_4 (xor_4_out, A3, B3);
  and and_3 (and_3_out, A2, B2);
  and and_4 (and_4_out, A3, B3);
  xor xor_5 (S0, xor_1_out, Cin);
  and and_5 (and_5_out, xor_1_out, Cin);
  xor xor_6 (S1, xor_2_out, Cin);
  and and_6 (and_6_out, xor_2_out, Cin);
  xor xor_7 (S2, xor_3_out, Cin);
  and and_7 (and_7_out, xor_3_out, Cin);
  xor xor_8 (S3, xor_4_out, Cin);
  and and_8 (and_8_out, xor_4_out, Cin);
  or or_1 (C2, and_5_out, and_1_out);
  or or_2 (C2, and_6_out, and_2_out);
  or or_3 (C2, and_7_out, and_3_out);
  or or_4 (C2, and_8_out, and_4_out);

  assign C3 = C2;
  assign C4 = C2;
  assign Cout = C2;
endmodule
